// Logisim project t888.circ as structural Verilog: 4 circuits, main circuit t888
module t888 (
  input  [9:0] in_1,
  input  [7:0] in_2,
  input  [7:0] in_3,
  output [1:0] out_4
);

  wire [3:0] undriven;
  wire [7:0] pmu_1_bus_out, pmu_1_rom_address, rom_1_data;

  ROM #(.Select("low")) rom_1 (.addr(pmu_1_rom_address), .data(rom_1_data));
  PMU pmu_1 (
    .ROM_Address(pmu_1_rom_address), .ROM_Data(rom_1_data), .Bus_In(pmu_1_bus_out), .Bus_Out(pmu_1_bus_out),
    .command(in_2));
  ALU alu_1 (.DataBus(pmu_1_bus_out), .DataBus_2(pmu_1_bus_out), .State(out_4), .Control(in_1));
  RAM #(.Select("low")) ram_1 (
    .addr(in_3), .data(pmu_1_bus_out), .sel(undriven[0]), .clk(undriven[1]), .ld(undriven[2]),
    .clr(undriven[3]));
endmodule

module ALU (
  input  [7:0] DataBus,
  input  [9:0] Control,
  output [7:0] DataBus_2,
  output [1:0] State
);

  wire adder_2_cout, C_en_q, multiplexer_2_out, not_2_out, not_3_out, subtractor_2_bout, subtractor_3_bout,
       zerotest_1_iszero;
  wire [0:0] and_2_out;
  wire [7:0] Accum_q, adder_1_out, adder_2_out, and_1_out, controlled_buffer_1_out, Data_q,
       demultiplexer_1_out0, multiplexer_1_out, multiplexer_3_out, negator_1_out, not_1_out, or_1_out,
       subtractor_1_out, subtractor_2_out, subtractor_3_out, xor_1_out;

  Register #(.trigger("low"), .Select("low")) Data (
    .D(DataBus), .Q(Data_q), .clk(Control[0]), .clr(Control[1]));  // open: en
  Adder adder_1 (.a(Accum_q), .b(8'h1), .out(adder_1_out));  // open: cin, cout
  Subtractor subtractor_1 (.a(Accum_q), .b(8'h1), .out(subtractor_1_out));  // open: bin, bout
  Negator negator_1 (.in(Accum_q), .out(negator_1_out));
  assign not_1_out = ~Accum_q;  // NOT_Gate not_1, 8 bits wide
  Multiplexer #(.width(8), .enable("false")) multiplexer_1 (
    .in0(Data_q), .in1(Accum_q), .out(multiplexer_1_out), .sel(Control[3]));
  Adder adder_2 (.a(Accum_q), .b(Data_q), .out(adder_2_out), .cin(and_2_out[0]), .cout(adder_2_cout));
  Subtractor subtractor_2 (
    .a(Accum_q), .b(Data_q), .out(subtractor_2_out), .bin(and_2_out[0]), .bout(subtractor_2_bout));
  Subtractor subtractor_3 (
    .a(Data_q), .b(Accum_q), .out(subtractor_3_out), .bin(and_2_out[0]), .bout(subtractor_3_bout));
  assign and_1_out = Accum_q & Data_q;  // AND_Gate and_1, 8 bits wide
  assign or_1_out = Accum_q | Data_q;  // OR_Gate or_1, 8 bits wide
  assign xor_1_out = Accum_q ^ Data_q;  // XOR_Gate xor_1, 8 bits wide
  not not_2 (not_2_out, Control[8]);
  Register #(.width(1), .Select("high")) C_en (
    .D(Control[5]), .en(Control[4]), .Q(C_en_q), .clk(Control[0]), .clr(Control[1]));
  Multiplexer #(.select(3)) multiplexer_2 (
    .in1(adder_2_cout), .in2(subtractor_2_bout), .in3(subtractor_3_bout), .in5(Accum_q[7]), .in6(Accum_q[0]),
    .in7(Accum_q[0]), .out(multiplexer_2_out), .sel({Control[9], Control[7:6]}), .en(not_2_out));  // open: in0, in4
  and and_2 (and_2_out[0], C_en_q, State[1]);
  Register #(.width(1), .Select("high")) Carry (
    .D(multiplexer_2_out), .en(Control[2]), .Q(State[1]), .clk(Control[0]), .clr(Control[4]));
  Multiplexer #(.select(4), .width(8), .enable("false")) multiplexer_3 (
    .in0({8{1'b0}}), .in1({Accum_q[6:0], and_2_out[0]}), .in2({and_2_out[0], Accum_q[7:1]}),
    .in3({{2{Accum_q[7]}}, Accum_q[6:1]}), .in4(adder_1_out), .in5(subtractor_1_out), .in6(negator_1_out),
    .in7(not_1_out), .in8(multiplexer_1_out), .in9(adder_2_out), .in10(subtractor_2_out),
    .in11(subtractor_3_out), .in12(and_1_out), .in13(or_1_out), .in14(xor_1_out), .out(multiplexer_3_out),
    .sel(Control[9:6]));  // open: in15
  assign controlled_buffer_1_out = Control[2] ? multiplexer_3_out : 8'bz;  // Controlled_Buffer controlled_buffer_1
  Demultiplexer #(.width(8), .tristate("true")) demultiplexer_1 (
    .out0(demultiplexer_1_out0), .out1(DataBus_2), .in(controlled_buffer_1_out), .sel(Control[3]),
    .en(not_3_out));
  not not_3 (not_3_out, Control[0]);
  Register #(.width(1), .Select("high")) Zero (
    .D(zerotest_1_iszero), .en(Control[2]), .Q(State[0]), .clk(Control[0]), .clr(Control[1]));
  ZeroTest zerotest_1 (.Input(controlled_buffer_1_out), .IsZero(zerotest_1_iszero));
  Register #(.Select("low")) Accum (
    .D(demultiplexer_1_out0), .Q(Accum_q), .clk(Control[0]), .clr(Control[1]));  // open: en

  // Other names for the same wires on the sheet: clock = Control[0]; reset = Control[1]; ALU_enable = Control[2];
  //   output__accumulate__result = Control[3]; set_carry_mode_and_clear_carry = Control[4];
  //   enable_carry_in = Control[5]; op_select[3:0] = Control[9:6]

  // Notes on the sheet:
  //   Control: pull=down
  //   DataBus: pull=down
endmodule

module ZeroTest (
  input  [7:0] Input,
  output IsZero
);

  nor nor_1 (IsZero, Input[0], Input[1], Input[2], Input[3], Input[4], Input[5], Input[6], Input[7]);

  // Notes on the sheet:
  //   Input: pull=up
endmodule

module PMU (
  input  [7:0] Bus_In,
  input  [7:0] ROM_Data,
  input  [7:0] command,
  output [7:0] Bus_Out,
  output [7:0] ROM_Address
);

  wire and_1_out;
  wire [7:0] adder_1_out, multiplexer_1_out;

  Adder adder_1 (.a(ROM_Address), .b({{3{ROM_Data[5]}}, ROM_Data[4:0]}), .out(adder_1_out));  // open: cin, cout
  Multiplexer #(.select(2), .width(8), .enable("false")) multiplexer_1 (
    .in1(ROM_Data), .in2(Bus_In), .in3(adder_1_out), .out(multiplexer_1_out), .sel(command[7:6]));  // open: in0
  Multiplexer #(.width(8)) multiplexer_2 (
    .in0(ROM_Data), .in1(ROM_Address), .out(Bus_Out), .sel(command[0]), .en(and_1_out));
  and and_1 (and_1_out, command[2], command[1]);
  Counter counter_1 (
    .load(command[4]), .D(multiplexer_1_out), .count(command[5]), .Q(ROM_Address), .clk(command[2]),
    .clr(command[3]));  // open: carry, preset, down

  // Other names for the same wires on the sheet: busel = command[0]; busen = command[1]; clock = command[2];
  //   reset = command[3]; load = command[4]; en = command[5]; mode[1:0] = command[7:6]
endmodule
